# Fritzing sketch Untitled Sketch 3 (saved by Fritzing 0.9.3b)
breadboards: 1

parts:
  part = DRV 8825 Stepper Motor Carrier, High Current [part_number="DRV 8825"]  # not connected
  DRV_2 = DRV 8825 Stepper Motor Carrier, High Current [part_number="DRV 8825"]  # not connected
  DRV_3 = DRV 8825 Stepper Motor Carrier, High Current [part_number="DRV 8825"]  # not connected
  DRV_4 = DRV 8825 Stepper Motor Carrier, High Current [part_number="DRV 8825"]  # not connected
  DRV_5 = DRV 8825 Stepper Motor Carrier, High Current [part_number="DRV 8825"]  # not connected
  DRV_6 = DRV 8825 Stepper Motor Carrier, High Current [part_number="DRV 8825"]  # not connected
  C1 = Electrolytic Capacitor [capacitance=1µF package="100 mil [THT, electrolytic]"]
  C2 = Electrolytic Capacitor [capacitance=1µF package="100 mil [THT, electrolytic]"]
  C3 = Electrolytic Capacitor [capacitance=1µF package="100 mil [THT, electrolytic]"]
  C4 = Electrolytic Capacitor [capacitance=1µF package="100 mil [THT, electrolytic]"]
  C5 = Electrolytic Capacitor [capacitance=1µF package="100 mil [THT, electrolytic]"]
  C6 = Electrolytic Capacitor [capacitance=1µF package="100 mil [THT, electrolytic]"]
  M3 = Stepper Motor - Bipolar  # not connected
  M4 = Stepper Motor - Bipolar  # not connected
  M5 = Stepper Motor - Bipolar  # not connected
  M6 = Stepper Motor - Bipolar  # not connected
  M7 = Stepper Motor - Bipolar  # not connected
  M8 = Stepper Motor - Bipolar  # not connected
  Componente1 = Photon  # not connected
  Power_plug1 = Power plug

nets:
  N1: C1.-, C2.-, C3.-, C4.-, C5.-, C6.-, Power_plug1.VCC
  N2: C1.+, C2.+, C3.+, C4.+, C5.+, C6.+, Power_plug1.GND
